# Fritzing sketch WIFI (saved by Fritzing 0.9.4)
breadboards: 1

parts:
  U1 = ESP8266-01S [part_number=ESP8266]
  Part1 = Arduino Ethernet Shield (Rev3)
  LED1 = LED - 5mm [color="Red (633nm)" package="5 mm [THT]"]
  LED2 = LED - 5mm [color="Red (633nm)" package="5 mm [THT]"]

nets:
  N1: U1.RXD, Part1.TX/D1
  VCC: U1.VCC, Part1.3V3
  GND: U1.GND, Part1.GND, LED2.cathode
  N2: U1.TXD, Part1.RX/D0
  N3: Part1.SPI/D12, LED1.anode
  N4: Part1.SPI/D13, LED2.anode
